# Fritzing sketch Atmosmesh V2 WIP (saved by Fritzing 1.0.8)
perfboards: 1

parts:
  J2 = female pin header, 15 pins [form="♀ (female)"]
  U1 = ESP32 Dev_Kit [part_number=ESP32S-HiLetgo]
  J3 = female pin header, 15 pins [form="♀ (female)"]
  J4 = Screw terminal - 2 pins [package=THT]
  C5 = Electrolytic Capacitor [capacitance=10µF voltage=35V package="100 mil [THT, electrolytic]"]
  C1 = Tantalum Capacitor [capacitance=100nF voltage=35V package="100 mil [THT, tantalum]"]
  C2 = Electrolytic Capacitor [capacitance=100nF voltage=35V package="100 mil [THT, electrolytic]"]
  SHT41 = female pin header, 4 pins [form="♀ (female)"]
  C6 = Tantalum Capacitor [capacitance=220nF voltage=35V package="100 mil [THT, tantalum]"]
  C7 = Tantalum Capacitor [capacitance=220nF voltage=35V package="100 mil [THT, tantalum]"]
  VEML7707 = female pin header, 5 pins [form="♀ (female)"]
  R1 = Resistor [tolerance=±5% power=0.25W resistance=330 package=THT]
  R2 = Resistor [tolerance=±5% power=0.25W resistance=330 package=THT]
  J5 = Piezo Speaker
  J6 = female pin header, 3 pins [form="♀ (female)"]
  Q1 = NPN-Transistor [package="TO92 [THT]"]
  R3 = Resistor [tolerance=±5% power=0.25W resistance=10k package=THT]
  PIR = female pin header, 3 pins [form="♀ (female)"]

nets:
  N1: J2.pin1, U1.GPIO23
  N2: J2.pin2, U1.GPIO22, R2.Pin_0
  N3: J2.pin3, U1.GPIO01
  N4: J2.pin4, U1.GPIO03
  N5: J2.pin5, U1.GPIO21, R1.Pin_0
  N6: J2.pin6, U1.GPIO19
  N7: J2.pin7, U1.GPIO18
  N8: J2.pin8, U1.GPIO05
  N9: J2.pin9, U1.GPIO17
  N10: J2.pin10, U1.GPIO16
  N11: J2.pin11, U1.GPIO4
  N12: J2.pin12, U1.GPIO2
  N13: J2.pin13, U1.GPIO15
  N14: J2.pin14, U1.GND, J3.pin14, J4.pin2, C5.-, C1.-, C2.-, SHT41.pin3, C6.+, Q1.C, PIR.pin3
  N15: J2.pin15, U1.3.3, C1.+, C2.+, SHT41.pin4, C6.-, C7.-, VEML7707.pin1
  N16: U1.EN, J3.pin1
  N17: U1.GPIO36, J3.pin2
  N18: U1.GPIO39, J3.pin3
  N19: U1.GPIO34, J3.pin4
  N20: U1.GPIO35, J3.pin5
  N21: U1.GPIO32, J3.pin6
  N22: U1.GPIO33, J3.pin7, Q1.E
  N23: U1.GPIO25, J3.pin8
  N24: U1.GPIO26, J3.pin9
  N25: U1.GPIO27, J3.pin10
  N26: U1.GPIO14, J3.pin11
  N27: U1.GPIO12, J3.pin12
  N28: U1.GPIO13, J3.pin13
  N29: U1.VIN, J3.pin15, J4.pin1, C5.+
  N30: SHT41.pin1, VEML7707.pin4, R2.Pin_1
  N31: SHT41.pin2, VEML7707.pin5, R1.Pin_1
  N32: C7.+, VEML7707.pin3
  N33: J5.pin1, J6.pin1
  N34: J5.pin2, J6.pin3
  N35: Q1.B, R3.Pin_0
  N36: R3.Pin_1, PIR.pin2
